# Fritzing sketch joystick_turboC64 (saved by Fritzing 0.9.3b)
breadboards: 1

parts:
  X1 = DB9 Connector [package=db9]
  Part1 = Arduino Uno (Rev3)
  R1 = Resistor [tolerance=±5% resistance=100 package=THT]
  R2 = Resistor [tolerance=±5% resistance=100 package=THT]
  R3 = Resistor [tolerance=±5% resistance=100 package=THT]
  R4 = Resistor [tolerance=±5% resistance=100 package=THT]
  R5 = Resistor [tolerance=±5% resistance=100 package=THT]
  R6 = Resistor [tolerance=±5% resistance=330 package=THT]
  R7 = Resistor [tolerance=±5% resistance=330 package=THT]
  R8 = Resistor [tolerance=±5% resistance=330 package=THT]
  R9 = Resistor [tolerance=±5% resistance=330 package=THT]
  R10 = Resistor [tolerance=±5% resistance=330 package=THT]

nets:
  N1: X1.1, R5.Pin_0
  N2: X1.2, Part1.GND, R6.Pin_0, R7.Pin_0, R8.Pin_0, R9.Pin_0, R10.Pin_0
  N3: X1.3, Part1.5V
  N4: X1.6, R4.Pin_0
  N5: X1.7, R3.Pin_0
  N6: X1.8, R2.Pin_0
  N7: X1.9, R1.Pin_0
  N8: Part1.D8, R4.Pin_1, R9.Pin_1
  N9: Part1.D9_PWM, R3.Pin_1, R8.Pin_1
  N10: Part1.D10_PWM/SS, R2.Pin_1, R7.Pin_1
  N11: Part1.D11_PWM/MOSI, R1.Pin_1, R6.Pin_1
  N12: Part1.D2, R5.Pin_1, R10.Pin_1

notes:
  Turbo controller (C64)
  Serial port pinout
  https://www.c64-wiki.com/wiki/Control_Port
  _______________
  \ 1 2 3 4 5 /
  \ 6 7 8 9 /
  1 - Up
  2 - Down
  3 - Left
  4 - Rigth
  5 - Pad A
  6 - Button
  7 - GND
  8 - 5V
  9 - Pad B
